// Logisim project RISC processor.circ as structural Verilog: 12 circuits, main circuit main
module main (
  input  [7:0] in_1,
  input  [7:0] in_2,
  input  [7:0] in_3,
  input  [7:0] in_4,
  output [24:0] out_5,
  output [7:0] out_6,
  output [4:0] out_7,
  output [7:0] out_8,
  output [7:0] out_9,
  output [7:0] out_10,
  output [7:0] out_11
);

  wire ALU_Save, C_Save, CFlag, clk, INPort_R, not_1_out, not_2_out, not_3_out, OUTPort_W, PC_Update, Reg_R,
       Reg_W, SRAM_R, SRAM_W, Stack_R, Stack_W, T0, T1, T2, T3, T4, UpdatePC, Z_Save, ZFlag;
  wire [3:0] x, y, z;
  wire [7:0] ALU_Out, Dout_IN, Dout_INPort, Dout_SRAM, Dout_Stack, Imm, multiplexer_1_out, multiplexer_2_out,
       multiplexer_3_out, multiplexer_5_out, multiplexer_6_out, PC_D2, Rx, Ry;

  Clock clock_1 (.out(clk));
  Multiplexer #(.select(5), .width(8), .disabled(0), .enable("false")) multiplexer_1 (
    .in13(Imm), .in14(Imm), .in15(Imm), .in16(Imm), .in17(Imm), .in27(ALU_Out), .in28(ALU_Out),
    .out(multiplexer_1_out), .sel(out_7));  // open: in0, in1, in2, in3, in4, in5, in6, in7, in8, in9, in10, in11, in12, in18, in19, in20, in21, in22, in23, in24, in25, in26, in29, in30, in31
  Timing_Generator Timing (.clk(clk), .T0(T0), .T1(T1), .T2(T2), .T3(T3), .T4(T4));
  PC_Counter PC (
    .CAddress(multiplexer_1_out), .clk(clk), .PC_Enable(T0), .PC_Update(PC_Update), .PC(out_6), .PC_D2(PC_D2));  // open: PC_D1
  INPort INPort (
    .clk(clk), .External_Datain1(in_1), .External_Datain2(in_2), .External_Datain3(in_3), .R(INPort_R),
    .External_Datain4(in_4), .Current_Address(Imm), .INPort_Out(Dout_INPort));  // open: INPort1Dout1, INPort2Dout2, INPort3Dout3, INPort4Dout4
  Inst_mem ROM (
    .Address(out_6), .R(T0), .clk(clk), .Inst_mem_out(out_5), .Imm(Imm), .S2(y), .S1(x), .Destination(z),
    .OpCode(out_7));
  OUTPort OUTPort (
    .clk(clk), .W(OUTPort_W), .DataOUTPort(ALU_Out), .Current_Address(Imm), .DataOUT_Port1(out_8),
    .DataOUT_Port2(out_9), .DataOUT_Port3(out_10), .DataOUT_Port4(out_11));
  Multiplexer #(.select(5), .width(8), .disabled(0), .enable("false")) multiplexer_2 (
    .in11(Imm), .in12(Imm), .in22(Rx), .in23(Rx), .out(multiplexer_2_out), .sel(out_7));  // open: in0, in1, in2, in3, in4, in5, in6, in7, in8, in9, in10, in13, in14, in15, in16, in17, in18, in19, in20, in21, in24, in25, in26, in27, in28, in29, in30, in31
  data_mem SRAM (.R(SRAM_R), .Address(multiplexer_2_out), .Datain(ALU_Out), .clk(clk), .W(SRAM_W), .DataOUT(Dout_SRAM));
  Stack Stack (
    .Datain(ALU_Out), .clk(clk), .R(Stack_R), .W(Stack_W), .DataOUT(Dout_Stack));  // open: SPwritePTR, SPreadPTR
  not not_1 (not_1_out, CFlag);
  not not_2 (not_2_out, ZFlag);
  not not_3 (not_3_out, ZFlag);
  Multiplexer #(.select(5), .width(8), .disabled(0), .enable("false")) multiplexer_3 (
    .in1(ALU_Out), .in2(ALU_Out), .in3(ALU_Out), .in4(ALU_Out), .in5(ALU_Out), .in6(ALU_Out), .in7(ALU_Out),
    .in8(ALU_Out), .in9(ALU_Out), .in10(ALU_Out), .in11(Dout_SRAM), .in19(Dout_Stack), .in20(Dout_IN),
    .in22(Dout_SRAM), .in24(ALU_Out), .in25(ALU_Out), .in26(ALU_Out), .out(multiplexer_3_out), .sel(out_7));  // open: in0, in12, in13, in14, in15, in16, in17, in18, in21, in23, in27, in28, in29, in30, in31
  Multiplexer #(.select(5), .disabled(0)) multiplexer_4 (
    .in0(1'b0), .in1(1'b0), .in2(1'b0), .in3(1'b0), .in4(1'b0), .in5(1'b0), .in6(1'b0), .in7(1'b0),
    .in8(1'b0), .in9(1'b0), .in10(1'b0), .in11(1'b0), .in12(1'b0), .in13(1'b1), .in14(ZFlag),
    .in15(not_3_out), .in16(CFlag), .in17(not_1_out), .in18(1'b0), .in19(1'b0), .in20(1'b0), .in21(1'b0),
    .in22(1'b0), .in23(1'b0), .in24(1'b0), .in25(1'b0), .in26(1'b0), .in27(ZFlag), .in28(not_2_out),
    .in29(1'b0), .in30(1'b0), .in31(1'b0), .out(UpdatePC), .sel(out_7), .en(T4));
  Register_File Register_File (
    .Datain(multiplexer_3_out), .Reg_W(Reg_W), .Reg_R(Reg_R), .clk(clk), .AddressW(z), .AddressR1(x),
    .AddressR2(y), .Rx(Rx), .Ry(Ry));
  MUX_32_to_1__1_bit mux_32_to_1__1_bit_1 (.Inp32bit(32'h801000), .Sel(out_7), .E(T3), .Out(SRAM_W));
  MUX_32_to_1__1_bit mux_32_to_1__1_bit_2 (.Inp32bit(32'h400800), .Sel(out_7), .E(T3), .Out(SRAM_R));
  MUX_32_to_1__1_bit mux_32_to_1__1_bit_3 (.Inp32bit(32'h7e413fe), .Sel(out_7), .E(T1), .Out(Reg_R));
  MUX_32_to_1__1_bit mux_32_to_1__1_bit_4 (.Inp32bit(32'h7580ffe), .Sel(out_7), .E(T4), .Out(Reg_W));
  MUX_32_to_1__1_bit mux_32_to_1__1_bit_5 (.Inp32bit(32'h200000), .Sel(out_7), .E(T3), .Out(OUTPort_W));
  MUX_32_to_1__1_bit mux_32_to_1__1_bit_6 (.Inp32bit(32'h100000), .Sel(out_7), .E(T3), .Out(INPort_R));
  Multiplexer #(.select(5), .width(8), .disabled(0), .enable("false")) multiplexer_5 (
    .in0({8{1'b0}}), .in1(Rx), .in2(Rx), .in3(Rx), .in4(Rx), .in5(Rx), .in6(Rx), .in7(Rx), .in8(Rx),
    .in9(Rx), .in10({8{1'b0}}), .in11({8{1'b0}}), .in12(Rx), .in13({8{1'b0}}), .in14({8{1'b0}}),
    .in15({8{1'b0}}), .in16({8{1'b0}}), .in17({8{1'b0}}), .in18(Rx), .in19({8{1'b0}}), .in20({8{1'b0}}),
    .in21(Rx), .in22({8{1'b0}}), .in23({8{1'b0}}), .in24(Rx), .in25(Rx), .in26(Rx), .in27(PC_D2),
    .in28(PC_D2), .in29({8{1'b0}}), .in30({8{1'b0}}), .in31({8{1'b0}}), .out(multiplexer_5_out), .sel(out_7));
  Multiplexer #(.select(5), .width(8), .disabled(0), .enable("false")) multiplexer_6 (
    .in0({8{1'b0}}), .in1(Ry), .in2(Ry), .in3(Ry), .in4(Ry), .in5(Imm), .in6(Imm), .in7(Imm), .in8(Imm),
    .in9({8{1'b0}}), .in10(Imm), .in11({8{1'b0}}), .in12({8{1'b0}}), .in13({8{1'b0}}), .in14({8{1'b0}}),
    .in15({8{1'b0}}), .in16({8{1'b0}}), .in17({8{1'b0}}), .in18({8{1'b0}}), .in19({8{1'b0}}),
    .in20({8{1'b0}}), .in21({8{1'b0}}), .in22({8{1'b0}}), .in23(Ry), .in24(Ry), .in25(Ry), .in26(Ry),
    .in27({1'b0, Imm[6:0]}), .in28({1'b0, Imm[6:0]}), .in29({8{1'b0}}), .in30({8{1'b0}}), .in31({8{1'b0}}),
    .out(multiplexer_6_out), .sel(out_7));
  ALU ALU (
    .IMM7(Imm[7]), .Opcode(out_7), .Operand1(multiplexer_5_out), .Operand2(multiplexer_6_out),
    .ALU_Save(ALU_Save), .CFlag_Save(C_Save), .ZFlag_Save(Z_Save), .clk(clk), .ALU_Out(ALU_Out),
    .CarryFlag(CFlag), .ZeroFlag(ZFlag));  // open: ALU_Out_D1
  MUX_32_to_1__1_bit mux_32_to_1__1_bit_7 (.Inp32bit(32'h1fa417fe), .Sel(out_7), .E(T2), .Out(ALU_Save));
  MUX_32_to_1__1_bit mux_32_to_1__1_bit_8 (.Inp32bit(32'h70001fe), .Sel(out_7), .E(T2), .Out(Z_Save));
  MUX_32_to_1__1_bit mux_32_to_1__1_bit_9 (.Inp32bit(32'h7000110), .Sel(out_7), .E(T2), .Out(C_Save));
  MUX_32_to_1__1_bit mux_32_to_1__1_bit_10 (.Inp32bit(32'h40000), .Sel(out_7), .E(T3), .Out(Stack_W));
  MUX_32_to_1__1_bit mux_32_to_1__1_bit_11 (.Inp32bit(32'h80000), .Sel(out_7), .E(T3), .Out(Stack_R));

  // Other names for the same wires on the sheet: OPCODE[4:0] = out_7
endmodule

module Reg_Synch_W (
  input  [7:0] Din,
  input  W,
  input  clk,
  output [7:0] Dout
);

  Register register_1 (.D(Din), .en(W), .Q(Dout), .clk(clk), .clr(1'b0));
endmodule

module Register_File (
  input  [7:0] Datain,
  input  clk,
  input  [3:0] AddressR1,
  input  Reg_W,
  input  [3:0] AddressW,
  input  [3:0] AddressR2,
  input  Reg_R,
  output [7:0] Rx,
  output [7:0] Ry
);

  wire decoder_1_out0, decoder_1_out1, decoder_1_out2, decoder_1_out3, decoder_1_out4, decoder_1_out5,
       decoder_1_out6, decoder_1_out7, decoder_1_out8, decoder_1_out9, decoder_1_out10, decoder_1_out11,
       decoder_1_out12, decoder_1_out13, decoder_1_out14, decoder_1_out15;
  wire [7:0] D0, D1, D2, D3, D4, D5, D6, D7, D8, D9, D10, D11, D12, D13, D14, D15, multiplexer_1_out,
       multiplexer_2_out;

  Decoder #(.select(4), .disabled(0)) decoder_1 (
    .out0(decoder_1_out0), .out1(decoder_1_out1), .out2(decoder_1_out2), .out3(decoder_1_out3),
    .out4(decoder_1_out4), .out5(decoder_1_out5), .out6(decoder_1_out6), .out7(decoder_1_out7),
    .out8(decoder_1_out8), .out9(decoder_1_out9), .out10(decoder_1_out10), .out11(decoder_1_out11),
    .out12(decoder_1_out12), .out13(decoder_1_out13), .out14(decoder_1_out14), .out15(decoder_1_out15),
    .sel(AddressW), .en(Reg_W));
  Reg_Synch_W reg_synch_w_1 (.Din(Datain), .W(decoder_1_out0), .clk(clk), .Dout(D0));
  Reg_Synch_W reg_synch_w_2 (.Din(Datain), .W(decoder_1_out1), .clk(clk), .Dout(D1));
  Reg_Synch_W reg_synch_w_3 (.Din(Datain), .W(decoder_1_out2), .clk(clk), .Dout(D2));
  Reg_Synch_W reg_synch_w_4 (.Din(Datain), .W(decoder_1_out3), .clk(clk), .Dout(D3));
  Reg_Synch_W reg_synch_w_5 (.Din(Datain), .W(decoder_1_out4), .clk(clk), .Dout(D4));
  Reg_Synch_W reg_synch_w_6 (.Din(Datain), .W(decoder_1_out5), .clk(clk), .Dout(D5));
  Reg_Synch_W reg_synch_w_7 (.Din(Datain), .W(decoder_1_out6), .clk(clk), .Dout(D6));
  Reg_Synch_W reg_synch_w_8 (.Din(Datain), .W(decoder_1_out7), .clk(clk), .Dout(D7));
  Reg_Synch_W reg_synch_w_9 (.Din(Datain), .W(decoder_1_out8), .clk(clk), .Dout(D8));
  Reg_Synch_W reg_synch_w_10 (.Din(Datain), .W(decoder_1_out9), .clk(clk), .Dout(D9));
  Reg_Synch_W reg_synch_w_11 (.Din(Datain), .W(decoder_1_out10), .clk(clk), .Dout(D10));
  Reg_Synch_W reg_synch_w_12 (.Din(Datain), .W(decoder_1_out11), .clk(clk), .Dout(D11));
  Reg_Synch_W reg_synch_w_13 (.Din(Datain), .W(decoder_1_out12), .clk(clk), .Dout(D12));
  Reg_Synch_W reg_synch_w_14 (.Din(Datain), .W(decoder_1_out13), .clk(clk), .Dout(D13));
  Reg_Synch_W reg_synch_w_15 (.Din(Datain), .W(decoder_1_out14), .clk(clk), .Dout(D14));
  Reg_Synch_W reg_synch_w_16 (.Din(Datain), .W(decoder_1_out15), .clk(clk), .Dout(D15));
  Multiplexer #(.select(4), .width(8), .enable("false")) multiplexer_1 (
    .in0(D0), .in1(D1), .in2(D2), .in3(D3), .in4(D4), .in5(D5), .in6(D6), .in7(D7), .in8(D8), .in9(D9),
    .in10(D10), .in11(D11), .in12(D12), .in13(D13), .in14(D14), .in15(D15), .out(multiplexer_1_out),
    .sel(AddressR1));
  Multiplexer #(.select(4), .width(8), .enable("false")) multiplexer_2 (
    .in0(D0), .in1(D1), .in2(D2), .in3(D3), .in4(D4), .in5(D5), .in6(D6), .in7(D7), .in8(D8), .in9(D9),
    .in10(D10), .in11(D11), .in12(D12), .in13(D13), .in14(D14), .in15(D15), .out(multiplexer_2_out),
    .sel(AddressR2));
  Register register_1 (.D(multiplexer_1_out), .en(Reg_R), .Q(Rx), .clk(clk), .clr(1'b0));
  Register register_2 (.D(multiplexer_2_out), .en(Reg_R), .Q(Ry), .clk(clk), .clr(1'b0));
endmodule

module data_mem (
  input  R,
  input  [7:0] Address,
  input  [7:0] Datain,
  input  clk,
  input  W,
  output [7:0] DataOUT
);

  wire [7:0] ram_1_data;

  RAM #(.bus("separate")) ram_1 (
    .addr(Address), .din(Datain), .data(ram_1_data), .str(W), .sel(1'b1), .clk(clk), .ld(1'b1), .clr(1'b0));
  Register register_1 (.D(ram_1_data), .en(R), .Q(DataOUT), .clk(clk), .clr(1'b0));
endmodule

module Inst_mem (
  input  [7:0] Address,
  input  R,
  input  clk,
  output [24:0] Inst_mem_out,
  output [7:0] Imm,
  output [3:0] S2,
  output [3:0] S1,
  output [3:0] Destination,
  output [4:0] OpCode
);

  wire [24:0] rom_1_data;

  ROM #(.dataWidth(25)) rom_1 (.addr(Address), .data(rom_1_data), .sel(1'b1));
  Register #(.width(25)) register_1 (
    .D(rom_1_data), .en(R), .Q({Inst_mem_out[24:20], Destination, Inst_mem_out[15:8], Imm}), .clk(clk),
    .clr(1'b0));

  assign {Inst_mem_out[19:16], Inst_mem_out[7:0]} = {Destination, Imm};
  assign OpCode = Inst_mem_out[24:20];
  assign S1 = Inst_mem_out[15:12];
  assign S2 = Inst_mem_out[11:8];
endmodule

module PC_Counter (
  input  [7:0] CAddress,
  input  clk,
  input  PC_Enable,
  input  PC_Update,
  output [7:0] PC,
  output [7:0] PC_D2,
  output [7:0] PC_D1
);

  wire [7:0] adder_1_out, multiplexer_1_out, multiplexer_2_out;

  Multiplexer #(.width(8), .disabled(0), .enable("false")) multiplexer_1 (
    .in0({8{1'b0}}), .in1(8'h1), .out(multiplexer_1_out), .sel(PC_Enable));
  Adder adder_1 (.a(PC), .b(multiplexer_1_out), .out(adder_1_out), .cin(1'b0));  // open: cout
  Multiplexer #(.width(8), .disabled(0), .enable("false")) multiplexer_2 (
    .in0(adder_1_out), .in1(CAddress), .out(multiplexer_2_out), .sel(PC_Update));
  Register register_1 (.D(multiplexer_2_out), .en(1'b1), .Q(PC), .clk(clk), .clr(1'b0));
  Register register_2 (.D(PC), .en(1'b1), .Q(PC_D1), .clk(clk), .clr(1'b0));
  Register register_3 (.D(PC_D1), .en(1'b1), .Q(PC_D2), .clk(clk), .clr(1'b0));

  // Notes on the sheet:
  //   Comes from Imm or ALU_OUT(for JMP PCR)
endmodule

module Timing_Generator (
  input  clk,
  output T0,
  output T1,
  output T2,
  output T3,
  output T4
);

  wire [2:0] adder_1_out, multiplexer_1_out, register_1_q;

  Adder #(.width(3)) adder_1 (.a(register_1_q), .b(3'b001), .out(adder_1_out), .cin(1'b0));  // open: cout
  Multiplexer #(.width(3), .enable("false")) multiplexer_1 (
    .in0(adder_1_out), .in1(3'b000), .out(multiplexer_1_out), .sel(T4));
  Register #(.width(3)) register_1 (.D(multiplexer_1_out), .en(1'b1), .Q(register_1_q), .clk(clk), .clr(1'b0));
  Decoder #(.select(3), .enable("false")) decoder_1 (
    .out0(T0), .out1(T1), .out2(T2), .out3(T3), .out4(T4), .sel(register_1_q));  // open: out5, out6, out7
endmodule

module Stack (
  input  [7:0] Datain,
  input  clk,
  input  R,
  input  W,
  output [7:0] DataOUT,
  output [7:0] SPwritePTR,
  output [7:0] SPreadPTR
);

  wire or_1_out;
  wire [7:0] adder_1_out, multiplexer_1_out, multiplexer_2_out;

  Adder adder_1 (.a(SPwritePTR), .b(8'h1), .out(adder_1_out), .cin(1'b0));  // open: cout
  Subtractor subtractor_1 (.a(SPwritePTR), .b(8'h1), .out(SPreadPTR), .bin(1'b0));  // open: bout
  Multiplexer #(.select(2), .width(8), .disabled(0), .enable("false")) multiplexer_1 (
    .in0(SPwritePTR), .in1(adder_1_out), .in2(SPreadPTR), .in3(SPwritePTR), .out(multiplexer_1_out),
    .sel({R, W}));
  Register register_1 (.D(multiplexer_1_out), .en(or_1_out), .Q(SPwritePTR), .clk(clk), .clr(1'b0));
  or or_1 (or_1_out, W, R);
  data_mem data_mem_1 (.R(R), .Address(multiplexer_2_out), .Datain(Datain), .clk(clk), .W(W), .DataOUT(DataOUT));
  Multiplexer #(.select(2), .width(8), .enable("false")) multiplexer_2 (
    .in0({8{1'b0}}), .in1(SPwritePTR), .in2(SPreadPTR), .in3({8{1'b0}}), .out(multiplexer_2_out), .sel({R, W}));
endmodule

module INPort (
  input  clk,
  input  [7:0] External_Datain1,
  input  [7:0] External_Datain2,
  input  [7:0] External_Datain3,
  input  R,
  input  [7:0] External_Datain4,
  input  [7:0] Current_Address,
  output [7:0] INPort1Dout1,
  output [7:0] INPort_Out,
  output [7:0] INPort2Dout2,
  output [7:0] INPort3Dout3,
  output [7:0] INPort4Dout4
);

  wire comparator_1_eq, comparator_2_eq, comparator_3_eq, comparator_4_eq;
  wire [1:0] priority_encoder_1_out;
  wire [7:0] multiplexer_1_out;

  Reg_Synch_W reg_synch_w_1 (.Din(External_Datain1), .W(1'b1), .clk(clk), .Dout(INPort1Dout1));
  Reg_Synch_W reg_synch_w_2 (.Din(External_Datain2), .W(1'b1), .clk(clk), .Dout(INPort2Dout2));
  Reg_Synch_W reg_synch_w_3 (.Din(External_Datain3), .W(1'b1), .clk(clk), .Dout(INPort3Dout3));
  Reg_Synch_W reg_synch_w_4 (.Din(External_Datain4), .W(1'b1), .clk(clk), .Dout(INPort4Dout4));
  Comparator comparator_1 (.a(Current_Address), .b(8'hf1), .eq(comparator_1_eq));  // open: gt, lt
  Comparator comparator_2 (.a(Current_Address), .b(8'hf2), .eq(comparator_2_eq));  // open: gt, lt
  Comparator comparator_3 (.a(Current_Address), .b(8'hf3), .eq(comparator_3_eq));  // open: gt, lt
  Comparator comparator_4 (.a(Current_Address), .b(8'hf4), .eq(comparator_4_eq));  // open: gt, lt
  Priority_Encoder #(.select(2)) priority_encoder_1 (
    .in0(comparator_1_eq), .in1(comparator_2_eq), .in2(comparator_3_eq), .in3(comparator_4_eq),
    .out(priority_encoder_1_out), .en_in(1'b1));  // open: gs, en_out
  Multiplexer #(.select(2), .width(8), .disabled(0), .enable("false")) multiplexer_1 (
    .in0(INPort1Dout1), .in1(INPort2Dout2), .in2(INPort3Dout3), .in3(INPort4Dout4), .out(multiplexer_1_out),
    .sel(priority_encoder_1_out));
  Register register_1 (.D(multiplexer_1_out), .en(R), .Q(INPort_Out), .clk(clk), .clr(1'b0));
endmodule

module OUTPort (
  input  clk,
  input  W,
  input  [7:0] DataOUTPort,
  input  [7:0] Current_Address,
  output [7:0] DataOUT_Port1,
  output [7:0] DataOUT_Port2,
  output [7:0] DataOUT_Port3,
  output [7:0] DataOUT_Port4
);

  wire and_1_out, and_2_out, and_3_out, and_4_out, comparator_1_eq, comparator_2_eq, comparator_3_eq,
       comparator_4_eq;

  Comparator comparator_1 (.a(Current_Address), .b(8'hf8), .eq(comparator_1_eq));  // open: gt, lt
  Comparator comparator_2 (.a(Current_Address), .b(8'hf9), .eq(comparator_2_eq));  // open: gt, lt
  Comparator comparator_3 (.a(Current_Address), .b(8'hfa), .eq(comparator_3_eq));  // open: gt, lt
  Comparator comparator_4 (.a(Current_Address), .b(8'hfb), .eq(comparator_4_eq));  // open: gt, lt
  and and_1 (and_1_out, W, comparator_1_eq);
  and and_2 (and_2_out, W, comparator_2_eq);
  and and_3 (and_3_out, W, comparator_3_eq);
  and and_4 (and_4_out, W, comparator_4_eq);
  Register register_1 (.D(DataOUTPort), .en(and_1_out), .Q(DataOUT_Port1), .clk(clk), .clr(1'b0));
  Register register_2 (.D(DataOUTPort), .en(and_2_out), .Q(DataOUT_Port2), .clk(clk), .clr(1'b0));
  Register register_3 (.D(DataOUTPort), .en(and_3_out), .Q(DataOUT_Port3), .clk(clk), .clr(1'b0));
  Register register_4 (.D(DataOUTPort), .en(and_4_out), .Q(DataOUT_Port4), .clk(clk), .clr(1'b0));
endmodule

module ALU (
  input  IMM7,
  input  [4:0] Opcode,
  input  [7:0] Operand1,
  input  [7:0] Operand2,
  input  ALU_Save,
  input  CFlag_Save,
  input  ZFlag_Save,
  input  clk,
  output [7:0] ALU_Out_D1,
  output [7:0] ALU_Out,
  output CarryFlag,
  output ZeroFlag
);

  wire Cout, multiplexer_3_out, nor_1_out;
  wire [7:0] ADD_ans, AND_ans, ExOR_ans, LShift_ans, multiplexer_2_out, OR_ans, RShift_ans, xor_1_out;
  wire [7:7] multiplexer_1_out;

  Multiplexer #(.select(5), .disabled(0), .enable("false")) multiplexer_1 (
    .in0(1'b0), .in1(1'b0), .in2(1'b0), .in3(1'b0), .in4(1'b0), .in5(1'b0), .in6(1'b0), .in7(1'b0),
    .in8(1'b0), .in9(1'b0), .in10(1'b0), .in11(1'b0), .in12(1'b0), .in13(1'b0), .in14(1'b0), .in15(1'b0),
    .in16(1'b0), .in17(1'b0), .in18(1'b0), .in19(1'b0), .in20(1'b0), .in21(1'b0), .in22(1'b0), .in23(1'b0),
    .in24(1'b1), .in25(1'b0), .in26(1'b0), .in27(IMM7), .in28(IMM7), .in29(1'b0), .in30(1'b0), .in31(1'b0),
    .out(multiplexer_1_out[7]), .sel(Opcode));
  assign AND_ans = Operand1 & Operand2;  // AND_Gate and_1, 8 bits wide
  assign OR_ans = Operand1 | Operand2;  // OR_Gate or_1, 8 bits wide
  Shifter shifter_1 (.in(Operand1), .\dist (Operand2[2:0]), .out(LShift_ans));
  Shifter #(.shift("lr")) shifter_2 (.in(Operand1), .\dist (Operand2[2:0]), .out(RShift_ans));
  assign xor_1_out = {8{multiplexer_1_out[7]}} ^ Operand2;  // XOR_Gate xor_1, 8 bits wide
  assign ExOR_ans = Operand1 ^ Operand2;  // XOR_Gate xor_2, 8 bits wide
  Adder adder_1 (.a(Operand1), .b(xor_1_out), .out(ADD_ans), .cin(multiplexer_1_out[7]), .cout(Cout));
  Multiplexer #(.select(5), .width(8), .disabled(0), .enable("false")) multiplexer_2 (
    .in0(ADD_ans), .in1(ADD_ans), .in2(OR_ans), .in3(ExOR_ans), .in4(ADD_ans), .in5(ADD_ans), .in6(OR_ans),
    .in7(ExOR_ans), .in8(ADD_ans), .in9(ADD_ans), .in10(ADD_ans), .in11({8{1'b0}}), .in12(ADD_ans),
    .in13({8{1'b0}}), .in14({8{1'b0}}), .in15({8{1'b0}}), .in16({8{1'b0}}), .in17({8{1'b0}}), .in18(ADD_ans),
    .in19({8{1'b0}}), .in20({8{1'b0}}), .in21(ADD_ans), .in22({8{1'b0}}), .in23(ADD_ans), .in24(ADD_ans),
    .in25(RShift_ans), .in26(LShift_ans), .in27(ADD_ans), .in28(ADD_ans), .in29({8{1'b0}}), .in30({8{1'b0}}),
    .in31({8{1'b0}}), .out(multiplexer_2_out), .sel(Opcode));
  Multiplexer #(.select(5), .disabled(0), .enable("false")) multiplexer_3 (
    .in0(1'b0), .in1(1'b0), .in2(1'b0), .in3(1'b0), .in4(Cout), .in5(1'b0), .in6(1'b0), .in7(1'b0),
    .in8(Cout), .in9(1'b0), .in10(1'b0), .in11(1'b0), .in12(1'b0), .in13(1'b0), .in14(1'b0), .in15(1'b0),
    .in16(1'b0), .in17(1'b0), .in18(1'b0), .in19(1'b0), .in20(1'b0), .in21(1'b0), .in22(1'b0), .in23(1'b0),
    .in24(1'b0), .in25(Operand1[0]), .in26(Operand1[7]), .in27(1'b0), .in28(1'b0), .in29(1'b0), .in30(1'b0),
    .in31(1'b0), .out(multiplexer_3_out), .sel(Opcode));
  nor nor_1 (nor_1_out, multiplexer_2_out[0], multiplexer_2_out[1], multiplexer_2_out[2], multiplexer_2_out[3], multiplexer_2_out[4], multiplexer_2_out[5], multiplexer_2_out[6], multiplexer_2_out[7]);
  Register register_1 (.D(multiplexer_2_out), .en(ALU_Save), .Q(ALU_Out), .clk(clk), .clr(1'b0));
  Register #(.width(1)) register_2 (.D(multiplexer_3_out), .en(CFlag_Save), .Q(CarryFlag), .clk(clk), .clr(1'b0));
  Register #(.width(1)) register_3 (.D(nor_1_out), .en(ZFlag_Save), .Q(ZeroFlag), .clk(clk), .clr(1'b0));
  Register register_4 (.D(ALU_Out), .en(1'b1), .Q(ALU_Out_D1), .clk(clk), .clr(1'b0));

  // Other names for the same wires on the sheet: Rx0 = Operand1[0]; Rx7 = Operand1[7]
endmodule

module MUX_32_to_1__1_bit (
  input  [31:0] Inp32bit,
  input  [4:0] Sel,
  input  E,
  output Out
);

  Multiplexer #(.select(5), .disabled(0)) multiplexer_1 (
    .in0(Inp32bit[0]), .in1(Inp32bit[1]), .in2(Inp32bit[2]), .in3(Inp32bit[3]), .in4(Inp32bit[4]),
    .in5(Inp32bit[5]), .in6(Inp32bit[6]), .in7(Inp32bit[7]), .in8(Inp32bit[8]), .in9(Inp32bit[9]),
    .in10(Inp32bit[10]), .in11(Inp32bit[11]), .in12(Inp32bit[12]), .in13(Inp32bit[13]), .in14(Inp32bit[14]),
    .in15(Inp32bit[15]), .in16(Inp32bit[16]), .in17(Inp32bit[17]), .in18(Inp32bit[18]), .in19(Inp32bit[19]),
    .in20(Inp32bit[20]), .in21(Inp32bit[21]), .in22(Inp32bit[22]), .in23(Inp32bit[23]), .in24(Inp32bit[24]),
    .in25(Inp32bit[25]), .in26(Inp32bit[26]), .in27(Inp32bit[27]), .in28(Inp32bit[28]), .in29(Inp32bit[29]),
    .in30(Inp32bit[30]), .in31(Inp32bit[31]), .out(Out), .sel(Sel), .en(E));
endmodule
